// Logisim project LEG Processor.circ as structural Verilog: 16 circuits, main circuit main
module main (
  input  [7:0] P_input,
  input  RESET,
  output [7:0] P_output
);

  wire and_1_out, and_2_out, and_3_out, and_4_out, and_5_out, and_6_out, and_7_out, and_8_out, and_9_out,
       and_10_out, and_11_out, and_12_out, and_13_out, and_14_out, and_15_out, and_16_out, and_17_out,
       and_18_out, and_19_out, and_20_out, and_21_out, and_22_out, and_23_out, and_24_out, and_25_out,
       and_26_out, and_27_out, Clock1, comparator_1_eq, comparator_2_eq, comparator_3_eq, comparator_4_eq,
       comparator_5_eq, cond_eng_1_out_5, controlled_buffer_13_out, controlled_buffer_15_out,
       controlled_buffer_16_out, controlled_buffer_25_out, controlled_buffer_45_out,
       controlled_buffer_58_out, controlled_buffer_62_out, controlled_buffer_66_out,
       controlled_buffer_70_out, controlled_buffer_73_out, controlled_buffer_74_out,
       controlled_buffer_77_out, controlled_buffer_78_out, controlled_buffer_81_out,
       controlled_buffer_82_out, controlled_buffer_85_out, controlled_buffer_86_out,
       controlled_buffer_88_out, controlled_buffer_90_out, controlled_buffer_92_out,
       controlled_buffer_94_out, controlled_buffer_106_out, controlled_buffer_110_out,
       controlled_buffer_114_out, controlled_buffer_118_out, not_1_out, not_2_out, not_3_out, not_4_out,
       not_5_out, not_6_out, not_7_out, not_8_out, not_9_out, not_10_out, not_11_out, not_12_out, not_13_out,
       not_14_out, not_15_out, not_16_out, not_17_out, onedec_1_out_2, onedec_1_out_3, onedec_2_out_2,
       onedec_2_out_3, or_1_out, or_2_out, or_3_out, or_4_out, or_5_out, or_6_out, or_7_out, or_8_out,
       or_9_out, or_10_out, or_11_out, or_12_out, or_13_out, or_14_out, or_15_out, or_16_out, or_17_out,
       or_18_out, or_19_out, pull_resistor_5_node, pull_resistor_6_node, pull_resistor_13_node,
       pull_resistor_14_node, pull_resistor_24_node, pull_resistor_26_node, pull_resistor_28_node,
       pull_resistor_30_node, pull_resistor_45_node, pull_resistor_46_node, pull_resistor_47_node,
       pull_resistor_48_node, pull_resistor_49_node, pull_resistor_51_node, pull_resistor_53_node,
       pull_resistor_55_node, threedec_1_out_5, threedec_1_out_6, threedec_1_out_7, threedec_1_out_8,
       threedec_1_out_9, threedec_1_out_10, threedec_1_out_11, threedec_1_out_12, threedec_2_out_5,
       threedec_2_out_6, threedec_2_out_7, threedec_2_out_8, threedec_2_out_9, threedec_2_out_10,
       threedec_2_out_11, threedec_2_out_12, threedec_3_out_5, threedec_3_out_6, threedec_3_out_7,
       threedec_3_out_8, threedec_3_out_9, threedec_3_out_10, threedec_3_out_11, threedec_3_out_12,
       twodec_1_out_3, twodec_1_out_4, twodec_1_out_5, twodec_1_out_6, twodec_2_out_3, twodec_2_out_4,
       twodec_2_out_5, twodec_2_out_6, twodec_3_out_3, twodec_3_out_4, twodec_3_out_5, twodec_3_out_6,
       twodec_4_out_3, twodec_4_out_4, twodec_4_out_5, twodec_4_out_6, twodec_5_out_3, twodec_5_out_4,
       twodec_5_out_5, twodec_5_out_6, twodec_6_out_3, twodec_6_out_4, twodec_6_out_5, twodec_6_out_6;
  wire [7:0] binary_to_bcd_converter_2_p1, binary_to_bcd_converter_3_p1, controlled_buffer_3_out,
       controlled_buffer_8_out, controlled_buffer_14_out, controlled_buffer_19_out, controlled_buffer_48_out,
       controlled_buffer_50_out, controlled_buffer_51_out, controlled_buffer_53_out,
       controlled_buffer_54_out, controlled_buffer_56_out, controlled_buffer_59_out,
       controlled_buffer_63_out, controlled_buffer_67_out, controlled_buffer_71_out,
       controlled_buffer_75_out, controlled_buffer_79_out, controlled_buffer_83_out,
       controlled_buffer_87_out, controlled_buffer_89_out, controlled_buffer_91_out,
       controlled_buffer_93_out, controlled_buffer_95_out, controlled_buffer_107_out,
       controlled_buffer_111_out, controlled_buffer_115_out, controlled_buffer_119_out, conv168_1_out_2,
       conv168_2_out_2, pull_resistor_2_node, pull_resistor_3_node, pull_resistor_10_node,
       pull_resistor_15_node, pull_resistor_20_node, pull_resistor_22_node, small_ram_1_valout,
       small_ram_2_valout, small_ram_3_valout, small_ram_4_valout, small_ram_5_valout, small_ram_6_valout,
       small_ram_7_valout, small_ram_8_valout, small_ram_9_valout, small_ram_10_valout, small_ram_11_valout,
       small_ram_12_valout, small_ram_13_valout, small_ram_14_valout, small_ram_15_valout,
       small_ram_16_valout, small_reg_1_valout, small_reg_2_valout, small_reg_3_valout, small_reg_4_valout,
       small_reg_5_valout, small_reg_6_valout, small_reg_7_valout, small_reg_8_valout, stack_ram8_1_valout;
  wire [7:7] pull_resistor_7_node;
  wire [15:0] add16_1_val, conv816_1_out_2, stack_ram16_1_valout;
  wire [31:0] Program_data;

  Clock clock_1 (.out(Clock1));
  _7_Segment_Display u_7_segment_display_1 ();  // open: g, f, a, b, e, d, c, dp
  _7_Segment_Display u_7_segment_display_2 ();  // open: g, f, a, b, e, d, c, dp
  // BCD_to_7_Segment_decoder bcd_to_7_segment_decoder_1: pin names not known
  // BCD_to_7_Segment_decoder bcd_to_7_segment_decoder_2: pin names not known
  // Binary_to_BCD_converter #(.binvalue(8)) binary_to_bcd_converter_1: pin names not known; wires that end beside it: P_input
  _7_Segment_Display u_7_segment_display_3 ();  // open: g, f, a, b, e, d, c, dp
  // BCD_to_7_Segment_decoder bcd_to_7_segment_decoder_3: pin names not known
  _7_Segment_Display u_7_segment_display_4 ();  // open: g, f, a, b, e, d, c, dp
  // BCD_to_7_Segment_decoder bcd_to_7_segment_decoder_4: pin names not known
  // Binary_to_BCD_converter #(.binvalue(8)) binary_to_bcd_converter_2: pin names not known; wires that end beside it: binary_to_bcd_converter_2_p1
  _7_Segment_Display u_7_segment_display_5 ();  // open: g, f, a, b, e, d, c, dp
  // BCD_to_7_Segment_decoder bcd_to_7_segment_decoder_5: pin names not known
  // Binary_to_BCD_converter #(.binvalue(8)) binary_to_bcd_converter_3: pin names not known; wires that end beside it: binary_to_bcd_converter_3_p1
  _7_Segment_Display u_7_segment_display_6 ();  // open: g, f, a, b, e, d, c, dp
  // BCD_to_7_Segment_decoder bcd_to_7_segment_decoder_6: pin names not known
  // Binary_to_BCD_converter #(.binvalue(8)) binary_to_bcd_converter_4: pin names not known; wires that end beside it: P_output
  Pull_Resistor pull_resistor_1 (.node(P_output));
  _7_Segment_Display u_7_segment_display_7 ();  // open: g, f, a, b, e, d, c, dp
  // BCD_to_7_Segment_decoder bcd_to_7_segment_decoder_7: pin names not known
  _7_Segment_Display u_7_segment_display_8 ();  // open: g, f, a, b, e, d, c, dp
  // BCD_to_7_Segment_decoder bcd_to_7_segment_decoder_8: pin names not known
  _7_Segment_Display u_7_segment_display_9 ();  // open: g, f, a, b, e, d, c, dp
  // BCD_to_7_Segment_decoder bcd_to_7_segment_decoder_9: pin names not known
  _7_Segment_Display u_7_segment_display_10 ();  // open: g, f, a, b, e, d, c, dp
  // BCD_to_7_Segment_decoder bcd_to_7_segment_decoder_10: pin names not known
  _7_Segment_Display u_7_segment_display_11 ();  // open: g, f, a, b, e, d, c, dp
  // BCD_to_7_Segment_decoder bcd_to_7_segment_decoder_11: pin names not known
  _7_Segment_Display u_7_segment_display_12 ();  // open: g, f, a, b, e, d, c, dp
  // BCD_to_7_Segment_decoder bcd_to_7_segment_decoder_12: pin names not known
  ROM #(.addrWidth(16), .dataWidth(32)) Program (
    .addr({binary_to_bcd_converter_3_p1, binary_to_bcd_converter_2_p1}), .data(Program_data));
  Pull_Resistor pull_resistor_2 (.node(pull_resistor_2_node));
  Pull_Resistor pull_resistor_3 (.node(pull_resistor_3_node));
  assign P_output = pull_resistor_14_node ? pull_resistor_20_node : 8'bz;  // Controlled_Buffer controlled_buffer_1
  cond_eng cond_eng_1 (
    .Enable(twodec_1_out_4), .Instruction({{4{pull_resistor_7_node[7]}}, Program_data[27:24]}),
    .Arg_1(pull_resistor_3_node), .Arg_2(pull_resistor_2_node), .out_5(cond_eng_1_out_5));
  onedec onedec_1 (.s(and_4_out), .out_2(onedec_1_out_2), .out_3(onedec_1_out_3));
  assign pull_resistor_2_node = twodec_2_out_4 ? controlled_buffer_3_out : 8'bz;  // Controlled_Buffer controlled_buffer_2
  assign controlled_buffer_3_out = or_1_out ? P_input : 8'bz;  // Controlled_Buffer controlled_buffer_3
  or or_1 (or_1_out, twodec_2_out_4, twodec_3_out_4);
  Pull_Resistor pull_resistor_4 (.node(cond_eng_1_out_5));
  Pull_Resistor pull_resistor_5 (.node(pull_resistor_5_node));
  assign pull_resistor_5_node = and_5_out ? onedec_1_out_2 : 1'bz;  // Controlled_Buffer controlled_buffer_4
  stack_ram16 stack_ram16_1 (
    .Pop(onedec_1_out_3), .Push(pull_resistor_5_node), .C(Clock1), .Value(add16_1_val),
    .ValOut(stack_ram16_1_valout));
  add16 add16_1 (
    .arg1({binary_to_bcd_converter_3_p1, binary_to_bcd_converter_2_p1}), .arg2(16'h1), .val(add16_1_val));  // open: ci, co
  assign pull_resistor_3_node = twodec_3_out_4 ? controlled_buffer_3_out : 8'bz;  // Controlled_Buffer controlled_buffer_5
  // Probe on {binary_to_bcd_converter_3_p1, binary_to_bcd_converter_2_p1}
  assign pull_resistor_2_node = or_2_out ? stack_ram8_1_valout : 8'bz;  // Controlled_Buffer controlled_buffer_6
  or or_2 (or_2_out, and_8_out, twodec_2_out_5);
  or or_3 (or_3_out, twodec_2_out_5, and_8_out, twodec_3_out_5);
  stack_ram8 stack_ram8_1 (
    .Pop(or_3_out), .Push(or_4_out), .C(Clock1), .Value(controlled_buffer_14_out),
    .ValOut(stack_ram8_1_valout));
  or or_4 (or_4_out, and_7_out, twodec_4_out_5);
  Pull_Resistor pull_resistor_6 (.node(pull_resistor_6_node));
  Comparator comparator_1 (.a({8{1'b0}}), .b(Program_data[31:24]), .eq(comparator_1_eq));  // open: gt, lt
  Pull_Resistor pull_resistor_7 (.node(pull_resistor_7_node[7]));
  or or_5 (or_5_out, and_5_out, and_2_out);
  assign pull_resistor_3_node = twodec_3_out_5 ? stack_ram8_1_valout : 8'bz;  // Controlled_Buffer controlled_buffer_7
  and and_1 (and_1_out, comparator_1_eq, comparator_2_eq);
  Comparator comparator_2 (.a({8{1'b0}}), .b(Program_data[23:16]), .eq(comparator_2_eq));  // open: gt, lt
  twodec twodec_1 (
    .s0(Program_data[28]), .s1(Program_data[29]), .out_3(twodec_1_out_3), .out_4(twodec_1_out_4),
    .out_5(twodec_1_out_5), .out_6(twodec_1_out_6));
  conv168 conv168_1 (.in_1(stack_ram16_1_valout), .out_2(conv168_1_out_2));
  or or_6 (or_6_out, or_5_out, cond_eng_1_out_5, pull_resistor_13_node);
  assign controlled_buffer_8_out = and_5_out ? conv168_1_out_2 : 8'bz;  // Controlled_Buffer controlled_buffer_8
  assign controlled_buffer_8_out = and_2_out ? conv168_2_out_2 : 8'bz;  // Controlled_Buffer controlled_buffer_9
  not not_1 (not_1_out, and_5_out);
  not not_2 (not_2_out, and_2_out);
  and and_2 (and_2_out, and_1_out, and_3_out);
  and and_3 (and_3_out, comparator_3_eq, comparator_4_eq);
  Comparator comparator_3 (.a({8{1'b0}}), .b(Program_data[15:8]), .eq(comparator_3_eq));  // open: gt, lt
  Pull_Resistor pull_resistor_8 (.node({binary_to_bcd_converter_3_p1, binary_to_bcd_converter_2_p1}));
  assign pull_resistor_2_node = twodec_2_out_6 ? conv168_2_out_2 : 8'bz;  // Controlled_Buffer controlled_buffer_10
  assign pull_resistor_3_node = twodec_3_out_6 ? conv168_2_out_2 : 8'bz;  // Controlled_Buffer controlled_buffer_11
  conv168 conv168_2 (.in_1({binary_to_bcd_converter_3_p1, binary_to_bcd_converter_2_p1}), .out_2(conv168_2_out_2));
  small_count16 small_count16_1 (
    .c_or_o(or_6_out), .cl(not_3_out), .overwrite_val(conv816_1_out_2),
    .count_val({binary_to_bcd_converter_3_p1, binary_to_bcd_converter_2_p1}));
  assign controlled_buffer_8_out = controlled_buffer_13_out ? controlled_buffer_14_out : 8'bz;  // Controlled_Buffer controlled_buffer_12
  conv816 conv816_1 (.in_1(controlled_buffer_8_out), .out_2(conv816_1_out_2));
  assign controlled_buffer_13_out = not_1_out ? not_2_out : 1'bz;  // Controlled_Buffer controlled_buffer_13
  assign controlled_buffer_14_out = cond_eng_1_out_5 ? Program_data[7:0] : 8'bz;  // Controlled_Buffer controlled_buffer_14
  not not_3 (not_3_out, Clock1);
  Comparator comparator_4 (.a({8{1'b0}}), .b(Program_data[7:0]), .eq(comparator_4_eq));  // open: gt, lt
  not not_4 (not_4_out, and_2_out);
  assign controlled_buffer_15_out = not_4_out ? twodec_1_out_3 : 1'bz;  // Controlled_Buffer controlled_buffer_15
  assign controlled_buffer_16_out = and_2_out ? and_2_out : 1'bz;  // Controlled_Buffer controlled_buffer_16
  assign controlled_buffer_16_out = twodec_1_out_4 ? twodec_1_out_4 : 1'bz;  // Controlled_Buffer controlled_buffer_17
  and and_4 (and_4_out, Program_data[24], twodec_1_out_5);
  assign controlled_buffer_14_out = not_5_out ? pull_resistor_20_node : 8'bz;  // Controlled_Buffer controlled_buffer_18
  not not_5 (not_5_out, cond_eng_1_out_5);
  Pull_Resistor pull_resistor_9 (.node(controlled_buffer_15_out));
  and and_5 (and_5_out, twodec_1_out_5, Program_data[25]);
  and and_6 (and_6_out, and_5_out, not_6_out);
  assign controlled_buffer_19_out = and_6_out ? Program_data[23:16] : 8'bz;  // Controlled_Buffer controlled_buffer_19
  not not_6 (not_6_out, and_4_out);
  conv816 conv816_2 (.in_1(controlled_buffer_19_out), .out_2(stack_ram16_1_valout));
  assign pull_resistor_2_node = Program_data[31] ? Program_data[23:16] : 8'bz;  // Controlled_Buffer controlled_buffer_20
  not not_7 (not_7_out, Program_data[31]);
  Pull_Resistor pull_resistor_10 (.node(pull_resistor_10_node));
  assign pull_resistor_10_node = not_7_out ? Program_data[23:16] : 8'bz;  // Controlled_Buffer controlled_buffer_21
  not not_8 (not_8_out, twodec_2_out_3);
  twodec twodec_2 (
    .s0(pull_resistor_10_node[6]), .s1(pull_resistor_10_node[7]), .out_3(twodec_2_out_3),
    .out_4(twodec_2_out_4), .out_5(twodec_2_out_5), .out_6(twodec_2_out_6));
  threedec threedec_1 (
    .dis(or_8_out), .s0(pull_resistor_10_node[0]), .s1(pull_resistor_10_node[1]),
    .s2(pull_resistor_10_node[2]), .out_5(threedec_1_out_5), .out_6(threedec_1_out_6),
    .out_7(threedec_1_out_7), .out_8(threedec_1_out_8), .out_9(threedec_1_out_9), .out_10(threedec_1_out_10),
    .out_11(threedec_1_out_11), .out_12(threedec_1_out_12));
  Pull_Resistor pull_resistor_11 (.node(Program_data[31]));
  Pull_Resistor pull_resistor_12 (.node(Program_data[30]));
  or or_7 (or_7_out, Program_data[31], and_5_out);
  twodec twodec_3 (
    .s0(pull_resistor_15_node[6]), .s1(pull_resistor_15_node[7]), .out_3(twodec_3_out_3),
    .out_4(twodec_3_out_4), .out_5(twodec_3_out_5), .out_6(twodec_3_out_6));
  Pull_Resistor pull_resistor_13 (.node(pull_resistor_13_node));
  Pull_Resistor pull_resistor_14 (.node(pull_resistor_14_node));
  or or_8 (or_8_out, not_8_out, pull_resistor_10_node[5], or_7_out);
  not not_9 (not_9_out, twodec_1_out_6);
  assign pull_resistor_3_node = controlled_buffer_25_out ? Program_data[15:8] : 8'bz;  // Controlled_Buffer controlled_buffer_22
  not not_10 (not_10_out, controlled_buffer_25_out);
  Pull_Resistor pull_resistor_15 (.node(pull_resistor_15_node));
  assign pull_resistor_15_node = not_10_out ? Program_data[15:8] : 8'bz;  // Controlled_Buffer controlled_buffer_23
  not not_11 (not_11_out, twodec_3_out_3);
  assign pull_resistor_13_node = not_14_out ? twodec_4_out_6 : 1'bz;  // Controlled_Buffer controlled_buffer_24
  threedec threedec_2 (
    .dis(or_10_out), .s0(pull_resistor_15_node[0]), .s1(pull_resistor_15_node[1]),
    .s2(pull_resistor_15_node[2]), .out_5(threedec_2_out_5), .out_6(threedec_2_out_6),
    .out_7(threedec_2_out_7), .out_8(threedec_2_out_8), .out_9(threedec_2_out_9), .out_10(threedec_2_out_10),
    .out_11(threedec_2_out_11), .out_12(threedec_2_out_12));
  assign controlled_buffer_25_out = not_9_out ? Program_data[30] : 1'bz;  // Controlled_Buffer controlled_buffer_25
  Pull_Resistor pull_resistor_16 (.node(controlled_buffer_25_out));
  or or_9 (or_9_out, controlled_buffer_25_out, and_5_out);
  twodec twodec_4 (
    .s0(Program_data[6]), .s1(Program_data[7]), .out_3(twodec_4_out_3), .out_4(twodec_4_out_4),
    .out_5(twodec_4_out_5), .out_6(twodec_4_out_6));
  assign pull_resistor_14_node = not_14_out ? twodec_4_out_4 : 1'bz;  // Controlled_Buffer controlled_buffer_26
  or or_10 (or_10_out, not_11_out, pull_resistor_15_node[5], or_9_out);
  assign controlled_buffer_16_out = twodec_1_out_6 ? Program_data[30] : 1'bz;  // Controlled_Buffer controlled_buffer_27
  assign controlled_buffer_16_out = and_5_out ? and_5_out : 1'bz;  // Controlled_Buffer controlled_buffer_28
  Pull_Resistor pull_resistor_17 (.node(controlled_buffer_16_out));
  Pull_Resistor pull_resistor_18 (.node(Program_data[7:0]));
  not not_12 (not_12_out, twodec_4_out_3);
  threedec threedec_3 (
    .dis(or_11_out), .s0(Program_data[0]), .s1(Program_data[1]), .s2(Program_data[2]),
    .out_5(threedec_3_out_5), .out_6(threedec_3_out_6), .out_7(threedec_3_out_7), .out_8(threedec_3_out_8),
    .out_9(threedec_3_out_9), .out_10(threedec_3_out_10), .out_11(threedec_3_out_11),
    .out_12(threedec_3_out_12));
  or or_11 (or_11_out, not_12_out, Program_data[5], controlled_buffer_16_out);
  not not_13 (not_13_out, and_5_out);
  Pull_Resistor pull_resistor_19 (.node({{4{pull_resistor_7_node[7]}}, Program_data[27:24]}));
  not not_14 (not_14_out, twodec_1_out_4);
  and and_7 (and_7_out, Program_data[27], twodec_1_out_5, Program_data[26]);
  or or_12 (or_12_out, threedec_2_out_5, threedec_1_out_5);
  small_reg small_reg_1 (
    .c(Clock1), .load(or_12_out), .save(threedec_3_out_5), .valin(pull_resistor_20_node),
    .valout(small_reg_1_valout));
  or or_13 (or_13_out, threedec_2_out_6, threedec_1_out_6);
  small_reg small_reg_2 (
    .c(Clock1), .load(or_13_out), .save(threedec_3_out_6), .valin(pull_resistor_20_node),
    .valout(small_reg_2_valout));
  or or_14 (or_14_out, threedec_2_out_7, threedec_1_out_7);
  small_reg small_reg_3 (
    .c(Clock1), .load(or_14_out), .save(threedec_3_out_7), .valin(pull_resistor_20_node),
    .valout(small_reg_3_valout));
  or or_15 (or_15_out, threedec_2_out_8, threedec_1_out_8);
  small_reg small_reg_4 (
    .c(Clock1), .load(or_15_out), .save(threedec_3_out_8), .valin(pull_resistor_20_node),
    .valout(small_reg_4_valout));
  or or_16 (or_16_out, threedec_2_out_9, threedec_1_out_9);
  small_reg small_reg_5 (
    .c(Clock1), .load(or_16_out), .save(threedec_3_out_9), .valin(pull_resistor_20_node),
    .valout(small_reg_5_valout));
  or or_17 (or_17_out, threedec_2_out_10, threedec_1_out_10);
  small_reg small_reg_6 (
    .c(Clock1), .load(or_17_out), .save(threedec_3_out_10), .valin(pull_resistor_20_node),
    .valout(small_reg_6_valout));
  or or_18 (or_18_out, threedec_2_out_11, threedec_1_out_11);
  small_reg small_reg_7 (
    .c(Clock1), .load(or_18_out), .save(threedec_3_out_11), .valin(pull_resistor_20_node),
    .valout(small_reg_7_valout));
  or or_19 (or_19_out, threedec_2_out_12, threedec_1_out_12);
  small_reg small_reg_8 (
    .c(Clock1), .load(or_19_out), .save(threedec_3_out_12), .valin(pull_resistor_20_node),
    .valout(small_reg_8_valout));
  Pull_Resistor pull_resistor_20 (.node(pull_resistor_20_node));
  not not_15 (not_15_out, Program_data[26]);
  and and_8 (and_8_out, Program_data[27], twodec_1_out_5, not_15_out);
  assign pull_resistor_2_node = threedec_1_out_5 ? small_reg_1_valout : 8'bz;  // Controlled_Buffer controlled_buffer_29
  assign pull_resistor_3_node = threedec_2_out_5 ? small_reg_1_valout : 8'bz;  // Controlled_Buffer controlled_buffer_30
  assign pull_resistor_2_node = threedec_1_out_6 ? small_reg_2_valout : 8'bz;  // Controlled_Buffer controlled_buffer_31
  assign pull_resistor_3_node = threedec_2_out_6 ? small_reg_2_valout : 8'bz;  // Controlled_Buffer controlled_buffer_32
  assign pull_resistor_2_node = threedec_1_out_7 ? small_reg_3_valout : 8'bz;  // Controlled_Buffer controlled_buffer_33
  assign pull_resistor_3_node = threedec_2_out_7 ? small_reg_3_valout : 8'bz;  // Controlled_Buffer controlled_buffer_34
  assign pull_resistor_2_node = threedec_1_out_8 ? small_reg_4_valout : 8'bz;  // Controlled_Buffer controlled_buffer_35
  assign pull_resistor_3_node = threedec_2_out_8 ? small_reg_4_valout : 8'bz;  // Controlled_Buffer controlled_buffer_36
  assign pull_resistor_2_node = threedec_1_out_9 ? small_reg_5_valout : 8'bz;  // Controlled_Buffer controlled_buffer_37
  assign pull_resistor_3_node = threedec_2_out_9 ? small_reg_5_valout : 8'bz;  // Controlled_Buffer controlled_buffer_38
  assign pull_resistor_2_node = threedec_1_out_10 ? small_reg_6_valout : 8'bz;  // Controlled_Buffer controlled_buffer_39
  assign pull_resistor_3_node = threedec_2_out_10 ? small_reg_6_valout : 8'bz;  // Controlled_Buffer controlled_buffer_40
  assign pull_resistor_2_node = threedec_1_out_11 ? small_reg_7_valout : 8'bz;  // Controlled_Buffer controlled_buffer_41
  assign pull_resistor_3_node = threedec_2_out_11 ? small_reg_7_valout : 8'bz;  // Controlled_Buffer controlled_buffer_42
  assign pull_resistor_2_node = threedec_1_out_12 ? small_reg_8_valout : 8'bz;  // Controlled_Buffer controlled_buffer_43
  assign pull_resistor_3_node = threedec_2_out_12 ? small_reg_8_valout : 8'bz;  // Controlled_Buffer controlled_buffer_44
  assign controlled_buffer_45_out = not_13_out ? twodec_1_out_5 : 1'bz;  // Controlled_Buffer controlled_buffer_45
  assign pull_resistor_20_node = controlled_buffer_45_out ? pull_resistor_2_node : 8'bz;  // Controlled_Buffer controlled_buffer_46
  assign pull_resistor_20_node = twodec_1_out_6 ? controlled_buffer_54_out : 8'bz;  // Controlled_Buffer controlled_buffer_47
  alu alu_1 (
    .Enable(controlled_buffer_15_out), .Instruction({{4{pull_resistor_7_node[7]}}, Program_data[27:24]}),
    .Arg_1(pull_resistor_2_node), .Arg_2(pull_resistor_3_node), .out_5(pull_resistor_20_node));
  not not_16 (not_16_out, Program_data[30]);
  assign controlled_buffer_48_out = not_16_out ? Program_data[23:16] : 8'bz;  // Controlled_Buffer controlled_buffer_48
  assign controlled_buffer_48_out = Program_data[30] ? Program_data[7:0] : 8'bz;  // Controlled_Buffer controlled_buffer_49
  onedec onedec_2 (.s(Program_data[30]), .out_2(onedec_2_out_2), .out_3(onedec_2_out_3));
  assign controlled_buffer_50_out = and_9_out ? controlled_buffer_48_out : 8'bz;  // Controlled_Buffer controlled_buffer_50
  assign controlled_buffer_51_out = twodec_1_out_6 ? {{4{pull_resistor_7_node[7]}}, Program_data[27:24]} : 8'bz;  // Controlled_Buffer controlled_buffer_51
  and and_9 (and_9_out, twodec_1_out_6, comparator_5_eq);
  not not_17 (not_17_out, comparator_5_eq);
  assign controlled_buffer_50_out = not_17_out ? pull_resistor_3_node : 8'bz;  // Controlled_Buffer controlled_buffer_52
  Pull_Resistor pull_resistor_21 (.node(controlled_buffer_51_out));
  Comparator comparator_5 (.a(Program_data[15:8]), .b(8'h20), .eq(comparator_5_eq));  // open: gt, lt
  and and_10 (and_10_out, twodec_1_out_6, onedec_2_out_3);
  and and_11 (and_11_out, twodec_1_out_6, onedec_2_out_2);
  assign controlled_buffer_53_out = twodec_1_out_6 ? controlled_buffer_50_out : 8'bz;  // Controlled_Buffer controlled_buffer_53
  assign controlled_buffer_54_out = twodec_1_out_6 ? controlled_buffer_56_out : 8'bz;  // Controlled_Buffer controlled_buffer_54
  Pull_Resistor pull_resistor_22 (.node(pull_resistor_22_node));
  assign pull_resistor_22_node = twodec_1_out_6 ? pull_resistor_2_node : 8'bz;  // Controlled_Buffer controlled_buffer_55
  twodec twodec_5 (
    .s0(controlled_buffer_51_out[0]), .s1(controlled_buffer_51_out[1]), .out_3(twodec_5_out_3),
    .out_4(twodec_5_out_4), .out_5(twodec_5_out_5), .out_6(twodec_5_out_6));
  twodec twodec_6 (
    .s0(controlled_buffer_51_out[2]), .s1(controlled_buffer_51_out[3]), .out_3(twodec_6_out_3),
    .out_4(twodec_6_out_4), .out_5(twodec_6_out_5), .out_6(twodec_6_out_6));
  Pull_Resistor pull_resistor_23 (.node(controlled_buffer_53_out));
  and and_12 (and_12_out, twodec_5_out_3, twodec_6_out_3);
  and and_13 (and_13_out, twodec_5_out_3, twodec_6_out_4);
  and and_14 (and_14_out, twodec_5_out_3, twodec_6_out_5);
  and and_15 (and_15_out, twodec_5_out_3, twodec_6_out_6);
  assign controlled_buffer_56_out = pull_resistor_24_node ? small_ram_1_valout : 8'bz;  // Controlled_Buffer controlled_buffer_56
  Pull_Resistor pull_resistor_24 (.node(pull_resistor_24_node));
  assign pull_resistor_24_node = and_12_out ? and_11_out : 1'bz;  // Controlled_Buffer controlled_buffer_57
  assign controlled_buffer_58_out = and_12_out ? and_10_out : 1'bz;  // Controlled_Buffer controlled_buffer_58
  Pull_Resistor pull_resistor_25 (.node(controlled_buffer_58_out));
  assign controlled_buffer_59_out = controlled_buffer_58_out ? pull_resistor_22_node : 8'bz;  // Controlled_Buffer controlled_buffer_59
  assign controlled_buffer_56_out = pull_resistor_26_node ? small_ram_2_valout : 8'bz;  // Controlled_Buffer controlled_buffer_60
  Pull_Resistor pull_resistor_26 (.node(pull_resistor_26_node));
  assign pull_resistor_26_node = and_13_out ? and_11_out : 1'bz;  // Controlled_Buffer controlled_buffer_61
  assign controlled_buffer_62_out = and_13_out ? and_10_out : 1'bz;  // Controlled_Buffer controlled_buffer_62
  Pull_Resistor pull_resistor_27 (.node(controlled_buffer_62_out));
  assign controlled_buffer_63_out = controlled_buffer_62_out ? pull_resistor_22_node : 8'bz;  // Controlled_Buffer controlled_buffer_63
  assign controlled_buffer_56_out = pull_resistor_28_node ? small_ram_3_valout : 8'bz;  // Controlled_Buffer controlled_buffer_64
  Pull_Resistor pull_resistor_28 (.node(pull_resistor_28_node));
  assign pull_resistor_28_node = and_14_out ? and_11_out : 1'bz;  // Controlled_Buffer controlled_buffer_65
  assign controlled_buffer_66_out = and_14_out ? and_10_out : 1'bz;  // Controlled_Buffer controlled_buffer_66
  Pull_Resistor pull_resistor_29 (.node(controlled_buffer_66_out));
  assign controlled_buffer_67_out = controlled_buffer_66_out ? pull_resistor_22_node : 8'bz;  // Controlled_Buffer controlled_buffer_67
  assign controlled_buffer_56_out = pull_resistor_30_node ? small_ram_4_valout : 8'bz;  // Controlled_Buffer controlled_buffer_68
  Pull_Resistor pull_resistor_30 (.node(pull_resistor_30_node));
  assign pull_resistor_30_node = and_15_out ? and_11_out : 1'bz;  // Controlled_Buffer controlled_buffer_69
  assign controlled_buffer_70_out = and_15_out ? and_10_out : 1'bz;  // Controlled_Buffer controlled_buffer_70
  Pull_Resistor pull_resistor_31 (.node(controlled_buffer_70_out));
  assign controlled_buffer_71_out = controlled_buffer_70_out ? pull_resistor_22_node : 8'bz;  // Controlled_Buffer controlled_buffer_71
  Pull_Resistor pull_resistor_32 (.node(controlled_buffer_56_out));
  small_ram small_ram_1 (
    .load(pull_resistor_24_node), .save(controlled_buffer_58_out), .adr(controlled_buffer_53_out),
    .valin(controlled_buffer_59_out), .c(Clock1), .r(RESET), .valout(small_ram_1_valout));
  small_ram small_ram_2 (
    .load(pull_resistor_26_node), .save(controlled_buffer_62_out), .adr(controlled_buffer_53_out),
    .valin(controlled_buffer_63_out), .c(Clock1), .r(RESET), .valout(small_ram_2_valout));
  small_ram small_ram_3 (
    .load(pull_resistor_28_node), .save(controlled_buffer_66_out), .adr(controlled_buffer_53_out),
    .valin(controlled_buffer_67_out), .c(Clock1), .r(RESET), .valout(small_ram_3_valout));
  small_ram small_ram_4 (
    .load(pull_resistor_30_node), .save(controlled_buffer_70_out), .adr(controlled_buffer_53_out),
    .valin(controlled_buffer_71_out), .c(Clock1), .r(RESET), .valout(small_ram_4_valout));
  and and_16 (and_16_out, twodec_5_out_4, twodec_6_out_3);
  and and_17 (and_17_out, twodec_5_out_4, twodec_6_out_4);
  and and_18 (and_18_out, twodec_5_out_4, twodec_6_out_5);
  and and_19 (and_19_out, twodec_5_out_4, twodec_6_out_6);
  assign controlled_buffer_56_out = controlled_buffer_73_out ? small_ram_5_valout : 8'bz;  // Controlled_Buffer controlled_buffer_72
  assign controlled_buffer_73_out = and_16_out ? and_11_out : 1'bz;  // Controlled_Buffer controlled_buffer_73
  assign controlled_buffer_74_out = and_16_out ? and_10_out : 1'bz;  // Controlled_Buffer controlled_buffer_74
  Pull_Resistor pull_resistor_33 (.node(controlled_buffer_74_out));
  assign controlled_buffer_75_out = controlled_buffer_74_out ? pull_resistor_22_node : 8'bz;  // Controlled_Buffer controlled_buffer_75
  assign controlled_buffer_56_out = controlled_buffer_77_out ? small_ram_6_valout : 8'bz;  // Controlled_Buffer controlled_buffer_76
  assign controlled_buffer_77_out = and_17_out ? and_11_out : 1'bz;  // Controlled_Buffer controlled_buffer_77
  assign controlled_buffer_78_out = and_17_out ? and_10_out : 1'bz;  // Controlled_Buffer controlled_buffer_78
  Pull_Resistor pull_resistor_34 (.node(controlled_buffer_78_out));
  assign controlled_buffer_79_out = controlled_buffer_78_out ? pull_resistor_22_node : 8'bz;  // Controlled_Buffer controlled_buffer_79
  assign controlled_buffer_56_out = controlled_buffer_81_out ? small_ram_7_valout : 8'bz;  // Controlled_Buffer controlled_buffer_80
  assign controlled_buffer_81_out = and_18_out ? and_11_out : 1'bz;  // Controlled_Buffer controlled_buffer_81
  assign controlled_buffer_82_out = and_18_out ? and_10_out : 1'bz;  // Controlled_Buffer controlled_buffer_82
  Pull_Resistor pull_resistor_35 (.node(controlled_buffer_82_out));
  assign controlled_buffer_83_out = controlled_buffer_82_out ? pull_resistor_22_node : 8'bz;  // Controlled_Buffer controlled_buffer_83
  assign controlled_buffer_56_out = controlled_buffer_85_out ? small_ram_8_valout : 8'bz;  // Controlled_Buffer controlled_buffer_84
  assign controlled_buffer_85_out = and_19_out ? and_11_out : 1'bz;  // Controlled_Buffer controlled_buffer_85
  assign controlled_buffer_86_out = and_19_out ? and_10_out : 1'bz;  // Controlled_Buffer controlled_buffer_86
  Pull_Resistor pull_resistor_36 (.node(controlled_buffer_86_out));
  assign controlled_buffer_87_out = controlled_buffer_86_out ? pull_resistor_22_node : 8'bz;  // Controlled_Buffer controlled_buffer_87
  Pull_Resistor pull_resistor_37 (.node(controlled_buffer_73_out));
  Pull_Resistor pull_resistor_38 (.node(controlled_buffer_77_out));
  Pull_Resistor pull_resistor_39 (.node(controlled_buffer_81_out));
  Pull_Resistor pull_resistor_40 (.node(controlled_buffer_85_out));
  and and_20 (and_20_out, twodec_5_out_5, twodec_6_out_3);
  small_ram small_ram_5 (
    .load(controlled_buffer_73_out), .save(controlled_buffer_74_out), .adr(controlled_buffer_53_out),
    .valin(controlled_buffer_75_out), .c(Clock1), .r(RESET), .valout(small_ram_5_valout));
  and and_21 (and_21_out, twodec_5_out_5, twodec_6_out_4);
  small_ram small_ram_6 (
    .load(controlled_buffer_77_out), .save(controlled_buffer_78_out), .adr(controlled_buffer_53_out),
    .valin(controlled_buffer_79_out), .c(Clock1), .r(RESET), .valout(small_ram_6_valout));
  and and_22 (and_22_out, twodec_5_out_5, twodec_6_out_5);
  small_ram small_ram_7 (
    .load(controlled_buffer_81_out), .save(controlled_buffer_82_out), .adr(controlled_buffer_53_out),
    .valin(controlled_buffer_83_out), .c(Clock1), .r(RESET), .valout(small_ram_7_valout));
  and and_23 (and_23_out, twodec_5_out_5, twodec_6_out_6);
  small_ram small_ram_8 (
    .load(controlled_buffer_85_out), .save(controlled_buffer_86_out), .adr(controlled_buffer_53_out),
    .valin(controlled_buffer_87_out), .c(Clock1), .r(RESET), .valout(small_ram_8_valout));
  assign controlled_buffer_88_out = and_20_out ? and_10_out : 1'bz;  // Controlled_Buffer controlled_buffer_88
  Pull_Resistor pull_resistor_41 (.node(controlled_buffer_88_out));
  assign controlled_buffer_89_out = controlled_buffer_88_out ? pull_resistor_22_node : 8'bz;  // Controlled_Buffer controlled_buffer_89
  assign controlled_buffer_90_out = and_21_out ? and_10_out : 1'bz;  // Controlled_Buffer controlled_buffer_90
  Pull_Resistor pull_resistor_42 (.node(controlled_buffer_90_out));
  assign controlled_buffer_91_out = controlled_buffer_90_out ? pull_resistor_22_node : 8'bz;  // Controlled_Buffer controlled_buffer_91
  assign controlled_buffer_92_out = and_22_out ? and_10_out : 1'bz;  // Controlled_Buffer controlled_buffer_92
  Pull_Resistor pull_resistor_43 (.node(controlled_buffer_92_out));
  assign controlled_buffer_93_out = controlled_buffer_92_out ? pull_resistor_22_node : 8'bz;  // Controlled_Buffer controlled_buffer_93
  assign controlled_buffer_94_out = and_23_out ? and_10_out : 1'bz;  // Controlled_Buffer controlled_buffer_94
  Pull_Resistor pull_resistor_44 (.node(controlled_buffer_94_out));
  assign controlled_buffer_95_out = controlled_buffer_94_out ? pull_resistor_22_node : 8'bz;  // Controlled_Buffer controlled_buffer_95
  assign controlled_buffer_56_out = pull_resistor_45_node ? small_ram_9_valout : 8'bz;  // Controlled_Buffer controlled_buffer_96
  Pull_Resistor pull_resistor_45 (.node(pull_resistor_45_node));
  assign pull_resistor_45_node = and_20_out ? and_11_out : 1'bz;  // Controlled_Buffer controlled_buffer_97
  assign controlled_buffer_56_out = pull_resistor_46_node ? small_ram_10_valout : 8'bz;  // Controlled_Buffer controlled_buffer_98
  Pull_Resistor pull_resistor_46 (.node(pull_resistor_46_node));
  assign pull_resistor_46_node = and_21_out ? and_11_out : 1'bz;  // Controlled_Buffer controlled_buffer_99
  assign controlled_buffer_56_out = pull_resistor_47_node ? small_ram_11_valout : 8'bz;  // Controlled_Buffer controlled_buffer_100
  Pull_Resistor pull_resistor_47 (.node(pull_resistor_47_node));
  assign pull_resistor_47_node = and_22_out ? and_11_out : 1'bz;  // Controlled_Buffer controlled_buffer_101
  assign controlled_buffer_56_out = pull_resistor_48_node ? small_ram_12_valout : 8'bz;  // Controlled_Buffer controlled_buffer_102
  Pull_Resistor pull_resistor_48 (.node(pull_resistor_48_node));
  assign pull_resistor_48_node = and_23_out ? and_11_out : 1'bz;  // Controlled_Buffer controlled_buffer_103
  small_ram small_ram_9 (
    .load(pull_resistor_45_node), .save(controlled_buffer_88_out), .adr(controlled_buffer_53_out),
    .valin(controlled_buffer_89_out), .c(Clock1), .r(RESET), .valout(small_ram_9_valout));
  small_ram small_ram_10 (
    .load(pull_resistor_46_node), .save(controlled_buffer_90_out), .adr(controlled_buffer_53_out),
    .valin(controlled_buffer_91_out), .c(Clock1), .r(RESET), .valout(small_ram_10_valout));
  small_ram small_ram_11 (
    .load(pull_resistor_47_node), .save(controlled_buffer_92_out), .adr(controlled_buffer_53_out),
    .valin(controlled_buffer_93_out), .c(Clock1), .r(RESET), .valout(small_ram_11_valout));
  small_ram small_ram_12 (
    .load(pull_resistor_48_node), .save(controlled_buffer_94_out), .adr(controlled_buffer_53_out),
    .valin(controlled_buffer_95_out), .c(Clock1), .r(RESET), .valout(small_ram_12_valout));
  and and_24 (and_24_out, twodec_5_out_6, twodec_6_out_3);
  and and_25 (and_25_out, twodec_5_out_6, twodec_6_out_4);
  and and_26 (and_26_out, twodec_5_out_6, twodec_6_out_5);
  and and_27 (and_27_out, twodec_5_out_6, twodec_6_out_6);
  assign controlled_buffer_56_out = pull_resistor_49_node ? small_ram_13_valout : 8'bz;  // Controlled_Buffer controlled_buffer_104
  Pull_Resistor pull_resistor_49 (.node(pull_resistor_49_node));
  assign pull_resistor_49_node = and_24_out ? and_11_out : 1'bz;  // Controlled_Buffer controlled_buffer_105
  assign controlled_buffer_106_out = and_24_out ? and_10_out : 1'bz;  // Controlled_Buffer controlled_buffer_106
  Pull_Resistor pull_resistor_50 (.node(controlled_buffer_106_out));
  assign controlled_buffer_107_out = controlled_buffer_106_out ? pull_resistor_22_node : 8'bz;  // Controlled_Buffer controlled_buffer_107
  assign controlled_buffer_56_out = pull_resistor_51_node ? small_ram_14_valout : 8'bz;  // Controlled_Buffer controlled_buffer_108
  Pull_Resistor pull_resistor_51 (.node(pull_resistor_51_node));
  assign pull_resistor_51_node = and_25_out ? and_11_out : 1'bz;  // Controlled_Buffer controlled_buffer_109
  assign controlled_buffer_110_out = and_25_out ? and_10_out : 1'bz;  // Controlled_Buffer controlled_buffer_110
  Pull_Resistor pull_resistor_52 (.node(controlled_buffer_110_out));
  assign controlled_buffer_111_out = controlled_buffer_110_out ? pull_resistor_22_node : 8'bz;  // Controlled_Buffer controlled_buffer_111
  assign controlled_buffer_56_out = pull_resistor_53_node ? small_ram_15_valout : 8'bz;  // Controlled_Buffer controlled_buffer_112
  Pull_Resistor pull_resistor_53 (.node(pull_resistor_53_node));
  assign pull_resistor_53_node = and_26_out ? and_11_out : 1'bz;  // Controlled_Buffer controlled_buffer_113
  assign controlled_buffer_114_out = and_26_out ? and_10_out : 1'bz;  // Controlled_Buffer controlled_buffer_114
  Pull_Resistor pull_resistor_54 (.node(controlled_buffer_114_out));
  assign controlled_buffer_115_out = controlled_buffer_114_out ? pull_resistor_22_node : 8'bz;  // Controlled_Buffer controlled_buffer_115
  assign controlled_buffer_56_out = pull_resistor_55_node ? small_ram_16_valout : 8'bz;  // Controlled_Buffer controlled_buffer_116
  Pull_Resistor pull_resistor_55 (.node(pull_resistor_55_node));
  assign pull_resistor_55_node = and_27_out ? and_11_out : 1'bz;  // Controlled_Buffer controlled_buffer_117
  assign controlled_buffer_118_out = and_27_out ? and_10_out : 1'bz;  // Controlled_Buffer controlled_buffer_118
  Pull_Resistor pull_resistor_56 (.node(controlled_buffer_118_out));
  assign controlled_buffer_119_out = controlled_buffer_118_out ? pull_resistor_22_node : 8'bz;  // Controlled_Buffer controlled_buffer_119
  small_ram small_ram_13 (
    .load(pull_resistor_49_node), .save(controlled_buffer_106_out), .adr(controlled_buffer_53_out),
    .valin(controlled_buffer_107_out), .c(Clock1), .r(RESET), .valout(small_ram_13_valout));
  small_ram small_ram_14 (
    .load(pull_resistor_51_node), .save(controlled_buffer_110_out), .adr(controlled_buffer_53_out),
    .valin(controlled_buffer_111_out), .c(Clock1), .r(RESET), .valout(small_ram_14_valout));
  small_ram small_ram_15 (
    .load(pull_resistor_53_node), .save(controlled_buffer_114_out), .adr(controlled_buffer_53_out),
    .valin(controlled_buffer_115_out), .c(Clock1), .r(RESET), .valout(small_ram_15_valout));
  small_ram small_ram_16 (
    .load(pull_resistor_55_node), .save(controlled_buffer_118_out), .adr(controlled_buffer_53_out),
    .valin(controlled_buffer_119_out), .c(Clock1), .r(RESET), .valout(small_ram_16_valout));

  // Other names for the same wires on the sheet: Clock2 = Clock1; Clock3 = Clock1
endmodule

module cond_eng (
  input  Enable,
  input  [7:0] Instruction,
  input  [7:0] Arg_1,
  input  [7:0] Arg_2,
  output out_5
);

  wire and_1_out, and_2_out, comparator_1_eq, comparator_1_lt, or_1_out, xor_1_out;

  Comparator #(.mode("unsigned")) comparator_1 (
    .a(Arg_1), .b(Arg_2), .eq(comparator_1_eq), .lt(comparator_1_lt));  // open: gt
  and and_1 (and_1_out, comparator_1_eq, Instruction[0]);
  and and_2 (and_2_out, comparator_1_lt, Instruction[1]);
  or or_1 (or_1_out, and_2_out, and_1_out);
  assign out_5 = Enable ? xor_1_out : 1'bz;  // Controlled_Buffer controlled_buffer_1
  xor xor_1 (xor_1_out, Instruction[2], or_1_out);
endmodule

module alu (
  input  Enable,
  input  [7:0] Instruction,
  input  [7:0] Arg_1,
  input  [7:0] Arg_2,
  output [7:0] out_5
);

  wire and_1_out, and_3_out, decoder_1_out0, decoder_1_out1, decoder_1_out2, decoder_1_out3, decoder_1_out4,
       decoder_1_out5, decoder_1_out6, decoder_2_out0, decoder_2_out1, decoder_2_out2, decoder_2_out3,
       decoder_2_out4, decoder_2_out5, decoder_2_out6, decoder_2_out7, not_3_out, or_2_out;
  wire [2:0] bitselector_1_out, bitselector_2_out;
  wire [7:0] adder_1_out, and_2_out, controlled_buffer_1_out, divider_1_out, divider_1_rem,
       multiplexer_1_out, multiplier_1_out, nand_1_out, negator_1_out, nor_1_out, not_1_out, not_2_out,
       or_1_out, shifter_1_out, shifter_2_out, subtractor_1_out, xor_1_out, xor_2_out;

  and and_1 (and_1_out, Instruction[3], Enable);
  Decoder #(.select(3)) decoder_1 (
    .out0(decoder_1_out0), .out1(decoder_1_out1), .out2(decoder_1_out2), .out3(decoder_1_out3),
    .out4(decoder_1_out4), .out5(decoder_1_out5), .out6(decoder_1_out6), .sel(Instruction[2:0]),
    .en(and_1_out));  // open: out7
  assign and_2_out = Arg_1 & Arg_2;  // AND_Gate and_2, 8 bits wide
  assign controlled_buffer_1_out = decoder_1_out0 ? and_2_out : 8'bz;  // Controlled_Buffer controlled_buffer_1
  assign or_1_out = Arg_1 | Arg_2;  // OR_Gate or_1, 8 bits wide
  assign controlled_buffer_1_out = decoder_1_out1 ? or_1_out : 8'bz;  // Controlled_Buffer controlled_buffer_2
  assign not_1_out = ~Arg_1;  // NOT_Gate not_1, 8 bits wide
  assign controlled_buffer_1_out = decoder_1_out2 ? not_1_out : 8'bz;  // Controlled_Buffer controlled_buffer_3
  assign xor_1_out = Arg_1 ^ Arg_2;  // XOR_Gate xor_1, 8 bits wide
  assign controlled_buffer_1_out = decoder_1_out3 ? xor_1_out : 8'bz;  // Controlled_Buffer controlled_buffer_4
  assign nand_1_out = ~(Arg_1 & Arg_2);  // NAND_Gate nand_1, 8 bits wide
  assign controlled_buffer_1_out = decoder_1_out4 ? nand_1_out : 8'bz;  // Controlled_Buffer controlled_buffer_5
  assign nor_1_out = ~(Arg_1 | Arg_2);  // NOR_Gate nor_1, 8 bits wide
  assign controlled_buffer_1_out = decoder_1_out5 ? nor_1_out : 8'bz;  // Controlled_Buffer controlled_buffer_6
  assign xor_2_out = Arg_1 ^ Arg_2;  // XOR_Gate xor_2, 8 bits wide
  assign not_2_out = ~xor_2_out;  // NOT_Gate not_2, 8 bits wide
  assign controlled_buffer_1_out = decoder_1_out6 ? not_2_out : 8'bz;  // Controlled_Buffer controlled_buffer_7
  or or_2 (or_2_out, decoder_2_out6, decoder_2_out7);
  and and_3 (and_3_out, not_3_out, Enable);
  Decoder #(.select(3)) decoder_2 (
    .out0(decoder_2_out0), .out1(decoder_2_out1), .out2(decoder_2_out2), .out3(decoder_2_out3),
    .out4(decoder_2_out4), .out5(decoder_2_out5), .out6(decoder_2_out6), .out7(decoder_2_out7),
    .sel(Instruction[2:0]), .en(and_3_out));
  not not_3 (not_3_out, Instruction[3]);
  Adder adder_1 (.a(Arg_1), .b(Arg_2), .out(adder_1_out));  // open: cin, cout
  Subtractor subtractor_1 (.a(Arg_1), .b(Arg_2), .out(subtractor_1_out));  // open: bin, bout
  Multiplier multiplier_1 (.a(Arg_1), .b(Arg_2), .out(multiplier_1_out));  // open: cin, cout
  Shifter shifter_1 (.in(Arg_1), .\dist (bitselector_1_out), .out(shifter_1_out));
  BitSelector #(.group(3)) bitselector_1 (.in(Arg_2), .out(bitselector_1_out), .sel(2'b00));
  Shifter #(.shift("lr")) shifter_2 (.in(Arg_1), .\dist (bitselector_2_out), .out(shifter_2_out));
  BitSelector #(.group(3)) bitselector_2 (.in(Arg_2), .out(bitselector_2_out), .sel(2'b00));
  Negator negator_1 (.in(Arg_1), .out(negator_1_out));
  Divider divider_1 (.a(Arg_1), .b(multiplexer_1_out), .out(divider_1_out), .upper(Arg_1), .rem(divider_1_rem));
  Multiplexer #(.width(8)) multiplexer_1 (.in0({8{1'b1}}), .in1(Arg_2), .out(multiplexer_1_out));  // open: sel
  assign out_5 = Enable ? controlled_buffer_1_out : 8'bz;  // Controlled_Buffer controlled_buffer_8
  assign controlled_buffer_1_out = decoder_2_out0 ? adder_1_out : 8'bz;  // Controlled_Buffer controlled_buffer_9
  assign controlled_buffer_1_out = decoder_2_out1 ? subtractor_1_out : 8'bz;  // Controlled_Buffer controlled_buffer_10
  assign controlled_buffer_1_out = decoder_2_out2 ? multiplier_1_out : 8'bz;  // Controlled_Buffer controlled_buffer_11
  assign controlled_buffer_1_out = decoder_2_out3 ? shifter_1_out : 8'bz;  // Controlled_Buffer controlled_buffer_12
  assign controlled_buffer_1_out = decoder_2_out4 ? shifter_2_out : 8'bz;  // Controlled_Buffer controlled_buffer_13
  assign controlled_buffer_1_out = decoder_2_out5 ? negator_1_out : 8'bz;  // Controlled_Buffer controlled_buffer_14
  assign controlled_buffer_1_out = decoder_2_out6 ? divider_1_out : 8'bz;  // Controlled_Buffer controlled_buffer_15
  assign controlled_buffer_1_out = decoder_2_out7 ? divider_1_rem : 8'bz;  // Controlled_Buffer controlled_buffer_16
endmodule

module stack_ram8 (
  input  Pop,
  input  Push,
  input  C,
  input  [7:0] Value,
  output [7:0] ValOut
);

  wire and_1_out, comparator_1_eq, nor_1_out, not_1_out, or_1_out;
  wire [7:0] adder_1_out, adder_2_out, controlled_buffer_1_out, controlled_buffer_3_out,
       controlled_buffer_5_out, negator_1_out, ram_1_dout, register_1_q;

  nor nor_1 (nor_1_out, Pop, Push);
  Register register_1 (.D(adder_2_out), .en(or_1_out), .clk(C), .Q(register_1_q));  // open: clr
  or or_1 (or_1_out, Pop, Push);
  Negator negator_1 (.in(8'h1), .out(negator_1_out));
  Comparator comparator_1 (.a({8{1'b0}}), .b(register_1_q), .eq(comparator_1_eq));  // open: gt, lt
  assign controlled_buffer_1_out = Push ? register_1_q : 8'bz;  // Controlled_Buffer controlled_buffer_1
  assign controlled_buffer_1_out = Pop ? adder_2_out : 8'bz;  // Controlled_Buffer controlled_buffer_2
  RAM ram_1 (.addr(controlled_buffer_1_out), .we(Push), .oe(1'b1), .clk(C), .din(Value), .dout(ram_1_dout));
  assign controlled_buffer_3_out = nor_1_out ? adder_1_out : 8'bz;  // Controlled_Buffer controlled_buffer_3
  Adder adder_1 (.a(negator_1_out), .b(register_1_q), .out(adder_1_out));  // open: cin, cout
  not not_1 (not_1_out, comparator_1_eq);
  assign controlled_buffer_1_out = and_1_out ? controlled_buffer_3_out : 8'bz;  // Controlled_Buffer controlled_buffer_4
  and and_1 (and_1_out, not_1_out, nor_1_out);
  assign controlled_buffer_5_out = Pop ? 8'hfe : 8'bz;  // Controlled_Buffer controlled_buffer_5
  Pull_Resistor pull_resistor_1 (.node(controlled_buffer_5_out));
  Adder adder_2 (.a(controlled_buffer_5_out), .b(register_1_q), .out(adder_2_out), .cin(1'b1));  // open: cout
  assign ValOut = Pop ? ram_1_dout : 8'bz;  // Controlled_Buffer controlled_buffer_6
endmodule

module stack_ram16 (
  input  Pop,
  input  Push,
  input  C,
  input  [15:0] Value,
  output [15:0] ValOut
);

  wire and_1_out, comparator_1_eq, nor_1_out, not_1_out, or_1_out;
  wire [7:0] adder_1_out, adder_2_out, controlled_buffer_1_out, controlled_buffer_3_out,
       controlled_buffer_5_out, negator_1_out, register_1_q;
  wire [15:0] ram_1_dout;

  nor nor_1 (nor_1_out, Pop, Push);
  Register register_1 (.D(adder_2_out), .en(or_1_out), .clk(C), .Q(register_1_q));  // open: clr
  or or_1 (or_1_out, Pop, Push);
  Negator negator_1 (.in(8'h1), .out(negator_1_out));
  Comparator comparator_1 (.a({8{1'b0}}), .b(register_1_q), .eq(comparator_1_eq));  // open: gt, lt
  assign controlled_buffer_1_out = Push ? register_1_q : 8'bz;  // Controlled_Buffer controlled_buffer_1
  assign controlled_buffer_1_out = Pop ? adder_2_out : 8'bz;  // Controlled_Buffer controlled_buffer_2
  RAM #(.dataWidth(16)) ram_1 (
    .addr(controlled_buffer_1_out), .we(Push), .oe(1'b1), .clk(C), .din(Value), .dout(ram_1_dout));
  assign controlled_buffer_3_out = nor_1_out ? adder_1_out : 8'bz;  // Controlled_Buffer controlled_buffer_3
  Adder adder_1 (.a(negator_1_out), .b(register_1_q), .out(adder_1_out));  // open: cin, cout
  not not_1 (not_1_out, comparator_1_eq);
  assign controlled_buffer_1_out = and_1_out ? controlled_buffer_3_out : 8'bz;  // Controlled_Buffer controlled_buffer_4
  and and_1 (and_1_out, not_1_out, nor_1_out);
  assign controlled_buffer_5_out = Pop ? 8'hfe : 8'bz;  // Controlled_Buffer controlled_buffer_5
  Pull_Resistor pull_resistor_1 (.node(controlled_buffer_5_out));
  Adder adder_2 (.a(controlled_buffer_5_out), .b(register_1_q), .out(adder_2_out), .cin(1'b1));  // open: cout
  Pull_Resistor pull_resistor_2 (.node(ValOut));
  assign ValOut = Pop ? ram_1_dout : 16'bz;  // Controlled_Buffer controlled_buffer_6
endmodule

module small_count (
  input  c_or_o,
  input  cl,
  input  [7:0] overwrite_val,
  output [7:0] count_val
);

  Counter counter_1 (.load(c_or_o), .clk(cl), .D(overwrite_val), .Q(count_val));  // open: clr, up, count, carry
endmodule

module small_count16 (
  input  c_or_o,
  input  cl,
  input  [15:0] overwrite_val,
  output [15:0] count_val
);

  Counter #(.max('hffff), .width(16)) counter_1 (
    .load(c_or_o), .clk(cl), .D(overwrite_val), .Q(count_val));  // open: clr, up, count, carry
endmodule

module onedec (
  input  s,
  output out_2,
  output out_3
);

  not not_1 (out_2, s);

  assign out_3 = s;
endmodule

module twodec (
  input  s0,
  input  s1,
  output out_3,
  output out_4,
  output out_5,
  output out_6
);

  Decoder #(.enable("false"), .select(2)) decoder_1 (
    .out0(out_3), .out1(out_4), .out2(out_5), .out3(out_6), .sel({s1, s0}));
endmodule

module threedec (
  input  dis,
  input  s0,
  input  s1,
  input  s2,
  output out_5,
  output out_6,
  output out_7,
  output out_8,
  output out_9,
  output out_10,
  output out_11,
  output out_12
);

  wire not_1_out;

  not not_1 (not_1_out, dis);
  Decoder #(.select(3)) decoder_1 (
    .out0(out_5), .out1(out_6), .out2(out_7), .out3(out_8), .out4(out_9), .out5(out_10), .out6(out_11),
    .out7(out_12), .sel({s2, s1, s0}), .en(not_1_out));
endmodule

module add8 (
  input  ci,
  input  [7:0] arg1,
  input  [7:0] arg2,
  output [7:0] val,
  output co
);

  Adder adder_1 (.a(arg1), .b(arg2), .out(val), .cin(ci), .cout(co));
endmodule

module add16 (
  input  ci,
  input  [15:0] arg1,
  input  [15:0] arg2,
  output [15:0] val,
  output co
);

  Adder #(.width(16)) adder_1 (.a(arg1), .b(arg2), .out(val), .cin(ci), .cout(co));
endmodule

module small_reg (
  input  load,
  input  save,
  input  [7:0] valin,
  input  c,
  output [7:0] valout
);

  wire [7:0] register_1_q;

  Register register_1 (.D(valin), .en(save), .clk(c), .Q(register_1_q));  // open: clr
  assign valout = load ? register_1_q : 8'bz;  // Controlled_Buffer controlled_buffer_1
endmodule

module small_ram (
  input  load,
  input  save,
  input  [7:0] adr,
  input  [7:0] valin,
  input  c,
  input  r,
  output [7:0] valout
);

  wire or_1_out, or_2_out;

  or or_1 (or_1_out, load, r);
  or or_2 (or_2_out, c, r);
  RAM ram_1 (.addr(adr), .we(save), .oe(or_1_out), .clk(or_2_out), .din(valin), .dout(valout));
endmodule

module conv168 (
  input  [15:0] in_1,
  output [7:0] out_2
);


  assign out_2 = in_1[7:0];
endmodule

module conv816 (
  input  [7:0] in_1,
  output [15:0] out_2
);

  Pull_Resistor pull_resistor_1 (.node(out_2[15]));

  assign out_2[14:0] = {{7{out_2[15]}}, in_1};
endmodule
